# Fritzing sketch Schematic (saved by Fritzing 0.9.3b)
breadboards: 1

parts:
  Componente1 = STM32F407G-DISC1
  BT1 = Bluetooth HC-06u [package=THT]

nets:
  N1: Componente1.pin26, Componente1.pin76, BT1.GND
  N2: Componente1.pin73, Componente1.pin74, BT1.RXD
  N3: Componente1.pin77, BT1.VCC
  N4: Componente1.pin99, BT1.TXD

custom parts:
  STM32F407G-DISC1: The STM32F4DISCOVERY Discovery kit allows users to easily develop applications with the STM32F407VG high-performance microcontroller with the Arm® Cortex®-M4 32-bit core. It includes everything required either for beginners or experienced users to get started quickly. Based on STM32F407VG, it includes an ST-LINK/V2-A embedded debug tool, one STMEMS digital accelerometer, one digital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
  Bluetooth HC-06u: Bluetooth HC-06 - face up, pins down 16.5mm x 37.5mm PCB
